// Logisim project project1.circ as structural Verilog: 6 circuits, main circuit main
module \function  (
  input  [31:0] in_1,
  output [31:0] out_2
);

  wire fp_const_1_p1, multiplier_1_p3, multiplier_2_p3, multiplier_3_p3;

  // FP_Const fp_const_1: pin names not known; wires that end beside it: fp_const_1_p1
  // Multiplier multiplier_1: pin names not known; wires that end beside it: in_1, in_1, multiplier_1_p3
  // Multiplier multiplier_2: pin names not known; wires that end beside it: multiplier_1_p3, in_1, multiplier_2_p3
  // Multiplier multiplier_3: pin names not known; wires that end beside it: in_1, fp_const_1_p1, multiplier_3_p3
  // Subtractor subtractor_1: pin names not known; wires that end beside it: multiplier_2_p3, multiplier_3_p3, out_2
  // FP_Probe fp_probe_1: pin names not known; wires that end beside it: out_2

  // Notes on the sheet:
  //   -4x
  //   x^3
  //   x^3-4x
  //   result
endmodule

module main (
);

  wire ab0_1_out_3, and_1_out, and_2_out, and_3_out, and_4_out, and_5_out, and_6_out, clock_1_out,
       comparator_1_p3, comparator_2_p1, comparator_2_p3, comparator_2_p5, comparator_2_p6, comparator_2_p7,
       comparator_2_p8, d5_d1_out, d6_d1_out, decoder_1_out7, fafb0_1_out_3, fp_const_3_p1, fp_const_4_p1,
       fp_probe_2_p2, fp_probe_2_p3, not_1_out;
  wire [2:0] n0_out, register_6_q;
  wire [31:0] ab2_1_out_3, baep_1_out_3, comparator_1_p4, fp_const_1_p1, fp_const_2_p1, function_1_out_2,
       function_2_out_2, multiplexer_1_out, multiplexer_2_out, register_1_q, register_2_q, register_3_q,
       register_4_q;

  // FP_Const fp_const_1: pin names not known; wires that end beside it: fp_const_1_p1
  or d5_d1 (d5_d1_out, comparator_2_p7, comparator_2_p3);
  or d6_d1 (d6_d1_out, comparator_2_p8, comparator_2_p3);
  Clock clock_1 (.out(clock_1_out));
  Multiplexer #(.width(32), .enable("false")) multiplexer_1 (
    .in0(fp_const_1_p1), .in1(ab2_1_out_3), .out(multiplexer_1_out), .sel(comparator_2_p8));
  Register #(.width(32)) register_1 (
    .D(multiplexer_1_out), .en(d6_d1_out), .Q(register_1_q), .clk(clock_1_out));  // open: clr
  \function  function_1 (.out_2(function_1_out_2), .in_1(register_1_q));
  fafb0 fafb0_1 (.in_1(fp_const_1_p1), .in_2(fp_const_2_p1), .out_3(fafb0_1_out_3));
  baep baep_1 (.in_1(register_3_q), .in_2(register_1_q), .out_3(baep_1_out_3));
  Register #(.width(32)) register_2 (
    .D(function_1_out_2), .en(comparator_2_p5), .Q(register_2_q), .clk(clock_1_out));  // open: clr
  // FP_Const fp_const_2: pin names not known; wires that end beside it: fp_const_2_p1
  // FP_Probe fp_probe_1: pin names not known; wires that end beside it: register_1_q
  // FP_Const fp_const_3: pin names not known; wires that end beside it: fp_const_3_p1
  ab0 ab0_1 (.in_1(comparator_1_p4), .in_2(register_2_q), .out_3(ab0_1_out_3));
  // FP_Probe fp_probe_2: pin names not known; wires that end beside it: register_2_q, fp_probe_2_p2, fp_probe_2_p3
  Register #(.width(32)) register_3 (
    .D(multiplexer_2_out), .en(d5_d1_out), .Q(register_3_q), .clk(clock_1_out));  // open: clr
  // Comparator comparator_1: pin names not known; wires that end beside it: baep_1_out_3, fp_const_3_p1, comparator_1_p3, comparator_1_p4
  Register #(.width(32)) register_4 (
    .D(ab2_1_out_3), .en(decoder_1_out7), .Q(register_4_q), .clk(clock_1_out));  // open: clr
  Multiplexer #(.width(32), .enable("false")) multiplexer_2 (
    .in0(fp_const_2_p1), .in1(ab2_1_out_3), .out(multiplexer_2_out), .sel(comparator_2_p7));
  \function  function_2 (.out_2(function_2_out_2), .in_1(ab2_1_out_3));
  // FP_Probe fp_probe_3: pin names not known
  // Comparator comparator_2: pin names not known; wires that end beside it: comparator_2_p1, fp_probe_2_p2, comparator_2_p3, fp_probe_2_p3, comparator_2_p5, comparator_2_p6, comparator_2_p7, comparator_2_p8
  // FP_Const fp_const_4: pin names not known; wires that end beside it: fp_const_4_p1, comparator_1_p4, fp_const_4_p1
  // FP_Probe fp_probe_4: pin names not known; wires that end beside it: register_3_q
  ab2 ab2_1 (.in_1(register_3_q), .in_2(register_1_q), .out_3(ab2_1_out_3));
  Register #(.width(32)) register_5 (
    .D(function_2_out_2), .en(comparator_2_p5), .Q(comparator_1_p4), .clk(clock_1_out));  // open: clr
  // FP_Probe fp_probe_5: pin names not known; wires that end beside it: ab2_1_out_3
  // FP_Probe fp_probe_6: pin names not known; wires that end beside it: register_4_q
  and and_1 (and_1_out, fafb0_1_out_3, fp_probe_2_p2);
  and and_2 (and_2_out, comparator_2_p6, comparator_2_p1);
  or n0 (n0_out[0], fp_probe_2_p3, and_2_out, and_1_out, and_3_out);
  and and_3 (and_3_out, comparator_2_p6, ab0_1_out_3);
  and and_4 (and_4_out, comparator_2_p6, comparator_2_p1);
  not not_1 (not_1_out, ab0_1_out_3);
  or n1 (n0_out[1], comparator_2_p3, fp_probe_2_p3, and_4_out, and_5_out, comparator_2_p7, comparator_2_p8);
  and and_5 (and_5_out, comparator_2_p6, not_1_out);
  and and_6 (and_6_out, comparator_1_p3, fp_probe_2_p3);
  or n2 (n0_out[2], and_6_out, comparator_2_p5, comparator_2_p6);
  Register #(.width(3)) register_6 (.D(n0_out), .en(1'b1), .Q(register_6_q), .clk(clock_1_out));  // open: clr
  Decoder #(.select(3), .enable("false")) decoder_1 (
    .out0(fp_probe_2_p2), .out1(comparator_2_p3), .out2(fp_probe_2_p3), .out3(comparator_2_p5),
    .out4(comparator_2_p6), .out5(comparator_2_p7), .out6(comparator_2_p8), .out7(decoder_1_out7),
    .sel(register_6_q));

  // Notes on the sheet:
  //   sa
  //   fa
  //   eb
  //   b-a
  //   cl
  //   goi
  //   sb
  //   L
  //   b-a>0
  //   fc
  //   c
  //   R
  //   cl
  //   result
endmodule

module ab2 (
  input  [31:0] in_1,
  input  [31:0] in_2,
  output [31:0] out_3
);

  wire adder_1_p3, fp_const_1_p1;

  // Adder adder_1: pin names not known; wires that end beside it: in_1, in_2, adder_1_p3
  // FP_Const fp_const_1: pin names not known; wires that end beside it: fp_const_1_p1
  // Divider divider_1: pin names not known; wires that end beside it: adder_1_p3, fp_const_1_p1, out_3

  // Notes on the sheet:
  //   a+b
endmodule

module fafb0 (
  input  [31:0] in_1,
  input  [31:0] in_2,
  output out_3
);

  wire [31:0] function_1_out_2, function_2_out_2;

  \function  function_1 (.out_2(function_1_out_2), .in_1(in_1));
  \function  function_2 (.out_2(function_2_out_2), .in_1(in_2));
  xor xor_1 (out_3, function_1_out_2[31], function_2_out_2[31]);
endmodule

module baep (
  input  [31:0] in_1,
  input  [31:0] in_2,
  output [31:0] out_3
);

  wire comparator_1_p3, fp_const_1_p1, fp_const_2_p1;
  wire [31:0] multiplier_1_p3, subtractor_1_p3;

  // Subtractor subtractor_1: pin names not known; wires that end beside it: in_1, in_2, subtractor_1_p3
  // FP_Const fp_const_1: pin names not known; wires that end beside it: fp_const_1_p1
  // Comparator comparator_1: pin names not known; wires that end beside it: subtractor_1_p3, fp_const_1_p1, comparator_1_p3
  // FP_Const fp_const_2: pin names not known; wires that end beside it: fp_const_2_p1
  // Multiplier multiplier_1: pin names not known; wires that end beside it: subtractor_1_p3, fp_const_2_p1, multiplier_1_p3
  Multiplexer #(.width(32), .enable("false")) multiplexer_1 (
    .in0(subtractor_1_p3), .in1(multiplier_1_p3), .out(out_3), .sel(comparator_1_p3));
endmodule

module ab0 (
  input  [31:0] in_1,
  input  [31:0] in_2,
  output out_3
);

  xor xor_1 (out_3, in_1[31], in_2[31]);
endmodule
