// Logisim project gcd.circ as structural Verilog: 1 circuit, main circuit main
module main (
  input  \GOİ ,
  input  [31:0] in_2,
  input  [31:0] y
);

  wire and_1_out, and_2_out, and_3_out, and_4_out, and_5_out, clock_1_out, comparator_1_eq, d_ff_2_qn,
       decoder_1_out0, decoder_1_out1, decoder_1_out2, decoder_1_out3, decoder_1_out4, decoder_1_out5,
       decoder_1_out6, decoder_1_out7, idx_out, idy_out, not_1_out, not_2_out, or_1_out, or_2_out, or_3_out,
       subtractor_1_bout;
  wire [2:0] d_ff_3_q;
  wire [31:0] multiplexer_1_out, multiplexer_2_out, multiplexer_3_out, multiplexer_4_out, subtractor_1_out,
       x_q, y_q;

  Clock clock_1 (.out(clock_1_out));
  Register #(.width(32)) register_1 (.D(multiplexer_2_out), .en(decoder_1_out5), .clk(clock_1_out));  // open: Q, clr
  Multiplexer #(.width(32), .enable("false")) multiplexer_1 (
    .in0(in_2), .in1(subtractor_1_out), .out(multiplexer_1_out), .sel(decoder_1_out3));
  Multiplexer #(.width(32), .enable("false")) multiplexer_2 (
    .in0(x_q), .in1(y_q), .out(multiplexer_2_out), .sel(decoder_1_out4));
  or idy (idy_out, decoder_1_out1, decoder_1_out4);
  or idx (idx_out, decoder_1_out1, decoder_1_out3);
  Register #(.width(32)) x (.D(multiplexer_1_out), .en(idx_out), .Q(x_q), .clk(clock_1_out));  // open: clr
  Multiplexer #(.width(32), .enable("false")) multiplexer_3 (
    .in0(y), .in1(subtractor_1_out), .out(multiplexer_3_out), .sel(decoder_1_out4));
  Multiplexer #(.width(32), .enable("false")) multiplexer_4 (
    .in0(y_q), .in1(x_q), .out(multiplexer_4_out), .sel(decoder_1_out4));
  Subtractor #(.width(32)) subtractor_1 (
    .a(multiplexer_2_out), .b(multiplexer_4_out), .out(subtractor_1_out), .bout(subtractor_1_bout));  // open: bin
  Register #(.width(32)) u_y (.D(multiplexer_3_out), .en(idy_out), .Q(y_q), .clk(clock_1_out));  // open: clr
  Comparator #(.width(32)) comparator_1 (.a(multiplexer_2_out), .b(y_q), .eq(comparator_1_eq));  // open: gt, lt
  not not_1 (not_1_out, comparator_1_eq);
  not not_2 (not_2_out, subtractor_1_bout);
  and and_1 (and_1_out, decoder_1_out2, or_1_out);
  or or_1 (or_1_out, subtractor_1_bout, comparator_1_eq);
  D_Flip_Flop d_ff_1 (.clk(clock_1_out), .D(and_1_out), .Q(d_ff_3_q[2]));  // open: Qn, preset, en, reset
  or or_2 (or_2_out, decoder_1_out1, and_2_out, decoder_1_out3, decoder_1_out4);
  and and_2 (and_2_out, decoder_1_out2, not_1_out, not_2_out);
  or or_3 (or_3_out, and_3_out, and_4_out, and_5_out);
  and and_3 (and_3_out, \GOİ , decoder_1_out0);
  and and_4 (and_4_out, decoder_1_out2, comparator_1_eq);
  D_Flip_Flop d_ff_2 (.clk(clock_1_out), .D(or_2_out), .Q(d_ff_3_q[1]), .Qn(d_ff_2_qn));  // open: preset, en, reset
  and and_5 (and_5_out, decoder_1_out2, not_1_out, not_2_out);
  D_Flip_Flop d_ff_3 (.clk(clock_1_out), .D(or_3_out), .Q(d_ff_3_q[0]));  // open: Qn, preset, en, reset
  Decoder #(.select(3), .enable("false")) decoder_1 (
    .out0(decoder_1_out0), .out1(decoder_1_out1), .out2(decoder_1_out2), .out3(decoder_1_out3),
    .out4(decoder_1_out4), .out5(decoder_1_out5), .out6(decoder_1_out6), .out7(decoder_1_out7), .sel(d_ff_3_q));
endmodule
